# Fritzing sketch water-level-sensor-drawing (saved by Fritzing 0.9.5d)
perfboards: 1

parts:
  A1 = Waveshare ESP32-C6 Touch LCD 1.47
  OLED1 = OLED 128x64 I2C Monochrome Display GND-VDD
  S1 = Pushbutton [package="[SMD]"]
  S2 = Pushbutton [package="[SMD]"]
  S3 = Pushbutton [package="[SMD]"]
  U1 = SWITCH_SPDT [package=kps-1290]
  A2 = A02YYUW  # not connected
  JACK1 = 2.1mm DC Barrel Jack
  JACK2 = 2.1mm DC Barrel Jack  # not connected
  JACK3 = 2.1mm DC Barrel Jack  # not connected

nets:
  N1: A1.Pin_8, S1.Pin_1, S1.Pin_2, S2.Pin_3, S2.Pin_4
  N2: A1.Pin_9, S3.Pin_1, S3.Pin_2
  N3: A1.Pin_12, OLED1.SDA
  N4: A1.Pin_13, OLED1.SCK
  N5: A1.Pin_15, S1.Pin_3, S1.Pin_4
  N6: A1.Pin_16, OLED1.VDD
  N7: A1.Pin_17, U1.S
  N8: S2.Pin_1, S2.Pin_2, S3.Pin_3, S3.Pin_4
  N9: U1.O, JACK1.switch

notes:
  USB C
  USB or DC Power 5V
  40 Meter 2 pair cable

custom parts:
  Waveshare ESP32-C6 Touch LCD 1.47: ESP32-C6 1.47inch Display Development Board, 172×320, 262K Color, 160MHz Running Frequency Single-core Processor, Supports WiFi 6 & Bluetooth, With Colorful RGB LED, ESP32 With Display.
  OLED 128x64 I2C Monochrome Display GND-VDD: OLED 128x64 I2C Monochrome Display. Note: there are two variants of this part, this one is the GND VDD SCK SDA variant. The other is VDD GND SCK SDA. Make sure you select the part that matches your module as using the incorrect part will probably destroy your module! In addition the mounting holes are marked on silkscreen but not by default drilled. If you want drilled mounting holes, copy a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
  A02YYUW: Ultrasonic distance sensor determines the distance to a target by measuring time lapses between the sending and receiving of the ultrasonic pulse.
  2.1mm DC Barrel Jack: 2.1mm DC Barrel Jack with Thru-Hole Connectors (breadboardable) (Mar 2019: replaced pads with standard pads with 0.042 in hole rather than the current 0.030 hole which is too small to mount the part)
